// Digital circuit CPU_main.dig as structural Verilog
module CPU_main (
  input  PC_out,
  input  Acc_out,
  input  ALU_out,
  input  IR_out
);

  wire [7:0] Acc_q, alu_main_1_p2, IR_q, PC_out_2, W_BUS;

  // Probe on W_BUS
  Register #(.Bits(8)) Acc (.Q(Acc_q));  // open: D, C, en
  ROM #(.AddrBits(8), .Bits(8)) ROM (.D(W_BUS));  // open: A, sel
  assign W_BUS = Acc_out ? Acc_q : 8'bz;  // Driver driver_1
  // ALU_main alu_main_1: pin names not known; wires that end beside it: W_BUS, alu_main_1_p2
  Register #(.Bits(8)) IR (.D(W_BUS), .Q(IR_q));  // open: C, en
  assign W_BUS = IR_out ? IR_q : 8'bz;  // Driver driver_2
  assign W_BUS = ALU_out ? alu_main_1_p2 : 8'bz;  // Driver driver_3
  Register #(.Bits(8)) B_reg (.D(W_BUS));  // open: C, en, Q
  Register #(.Bits(8)) Out_reg (.D(W_BUS));  // open: C, en, Q
  CounterPreset PC (.in(W_BUS[0]), .out(PC_out_2[0]));  // open: en, C, dir, ld, clr, ovf
  Register #(.Bits(8)) MAR (.D(W_BUS));  // open: C, en, Q
  assign W_BUS = PC_out ? PC_out_2 : 8'bz;  // Driver driver_4
  // Pins of 1 and 8 bits meet at W_BUS
  // Pins of 1 and 8 bits meet at PC_out_2
endmodule
